# Fritzing sketch nucleo-tmc5160bob-spi (saved by Fritzing 0.9.3b)

parts:
  J1 = STM32 Nucleo boards
  TMC5160-BOB1 = TMC5160-BOB [package=THT]

nets:
  N1: J1.PB12, TMC5160-BOB1.CS
  N2: J1.3V3, TMC5160-BOB1.VCC_IO
  N3: J1.GND, TMC5160-BOB1.GND#0, TMC5160-BOB1.GND#6, TMC5160-BOB1.DRV_ENN
  N4: J1.PB15, TMC5160-BOB1.SDI
  N5: J1.PB14, TMC5160-BOB1.SDO
  N6: J1.PB13, TMC5160-BOB1.SCK

custom parts:
  TMC5160-BOB: TMC5160-BOB stepper motor controller and driver eval board from TRINAMIC
