# Fritzing sketch nucleo-tmc5160eval-uart (saved by Fritzing 0.9.3b)

parts:
  J1 = STM32 Nucleo boards
  TMC5160-BOB2 = TMC5160-BOB [package=THT]
  R1 = Resistor [tolerance=±5% resistance=10k package=THT]

nets:
  N1: J1.GND, TMC5160-BOB2.GND#0, TMC5160-BOB2.GND#6, TMC5160-BOB2.SD_MODE
  N2: J1.3V3, R1.Pin_0
  N3: J1.5V, TMC5160-BOB2.+5V_USB
  N4: J1.PA9, TMC5160-BOB2.SWP_DIAG1, R1.Pin_1
  N5: TMC5160-BOB2.DRV_ENN, TMC5160-BOB2.GND#16
  N6: TMC5160-BOB2.+5V_VM, TMC5160-BOB2.SPI_MODE

custom parts:
  TMC5160-BOB: TMC5160-BOB stepper motor controller and driver eval board from TRINAMIC
