# Fritzing sketch nucleo-tmc5160ss-sd (saved by Fritzing 0.9.3b)

parts:
  J1 = STM32 Nucleo boards
  Mod1 = TMC5160 [package=THT]

nets:
  N1: J1.PB12, Mod1.CS_/_CFG3
  N2: J1.GND#881, Mod1.EN
  N3: J1.D9_PWM, Mod1.Dir
  N4: J1.D7, Mod1.Step
  N5: J1.3V3, Mod1.VIO
  N6: J1.GND#1189, Mod1.GND
  N7: J1.PB15, Mod1.SDI/CFG1
  N8: J1.PB14, Mod1.SDO_/_CFG0
  N9: J1.PB13, Mod1.SCK/CFG2

custom parts:
  TMC5160: TMC5160 stepper motor controller and driver.
